# Fritzing sketch FLuxLight (saved by Fritzing 0.7.12b)
breadboards: 1

parts:
  Arduino1 = Arduino
  IC1 = DS1302 [package="SO8 [SMD]"]
  Q2 = Basic FET N-Channel [package="TO220 [THT]"]
  Q3 = Basic FET N-Channel [package="TO220 [THT]"]
  Q4 = Basic FET N-Channel [package="TO220 [THT]"]
  S1 = Square Pushbutton
  LED1 = RGB LED (com. anode, rbg) [package="5 mm [THT]"]
  Power_plug1 = Power plug

nets:
  N1: Arduino1.D13, IC1.+V
  N2: Arduino1.D12, IC1.X1_-_Crystal
  N3: Arduino1.D11, IC1.X2_-_Crystal
  N4: Arduino1.D6, Q4.gate
  N5: Arduino1.D5, Q2.gate
  N6: Arduino1.D3, Q3.gate
  N7: Arduino1.+5V, IC1.0V
  GND: Arduino1.GND, IC1.CE_-_Chip_Enable, Q2.source, Q3.source, Q4.source, S1.leg1, Power_plug1.GND
  N8: Arduino1.A2, S1.leg0
  N9: Q2.drain, LED1.common_anode
  N10: Q3.drain, LED1.blue_cathode
  N11: Q4.drain, LED1.red_cathode
  N12: LED1.green_cathode, Power_plug1.VCC

notes:
  12v power supply
  RGB led stip
